# Fritzing sketch Physical-Layout_Prototype (saved by Fritzing 1.0.6)
circuit board: 8.46667cm x 5.64444cm
breadboards: 1

parts:
  U1 = ATTiny84 [package=dip]
  VCC1 = 4 x AAA Battery Mount [internal_resistance=0.1Ω]
  R4 = Rotary Potentiometer (Large) [maximum_resistance=10kΩ knob_status=50% power=0.5W package=THT]
  LED1 = LED - 5mm [color="Green (565nm)" current=0.030A package="5 mm [THT]"]
  U2 = TMP36 [package=to-92]
  C2 = Capacitor [package=cap-pth-small2]
  LED2 = LED - 5mm [color="Blue (505nm)" current=0.030A package="5 mm [THT]"]
  LED3 = LED - 5mm [color="Orange (612nm)" current=0.030A package="5 mm [THT]"]
  R6 = Resistor [tolerance=±5% power=0.25W resistance=220 package=THT]
  R7 = Resistor [tolerance=±5% power=0.25W resistance=220 package=THT]
  R5 = Resistor [tolerance=±5% power=0.25W resistance=330 package=THT]  # not connected

nets (from the pcb view):
  N1: U1.pin1, VCC1.+, R4.leg1, U2.GND, C2.1
  N2: U1.pin3, R6.Pin_0
  N3: U1.pin5, R7.Pin_0
  N4: U1.pin6, U2.VOUT
  N5: U1.pin10, R4.wiper
  N6: U1.pin14, R4.leg2, LED1.cathode, U2.VCC, LED2.cathode, LED3.cathode
  N7: VCC1.-, C2.2
  N8: LED1.anode, R6.Pin_1
  N9: LED3.anode, R7.Pin_1

notes:
  Temp-Sense Pin 6 .............. | PIN_PA7
  Temp-Set ...... Pin 10 ............ | PIN_PA3
  LED Below..... Pin 13 ............ | PIN_PA0
  LED In Band Pin 5 .............. | PIN_PB2
  LED Above .... Pin 3 .............. | PIN_PB1
  SSR Trigger .. Pin 2 .............. | PIN_PB0
  TM19 Sensor IC
  10K Pot for setting desired temperature
  0.1uF
  330
  220
  5 Volts DC Power Source

custom parts:
  ATTiny84: Atmel ATTiny84 processor. 8 ADC pins, 4 PWM pins. Available in either 10MHz or 20MHz. The last 2 pin numbers refer to arduino. D6 = Arduino 6, A6 = Arduino A6 example: PA6 (SDA/MOSI/OC1A/DI/AD6/PCINT6/D6/A6) NOTE: This part is diagrammed to suit the MIT HLT ATTiny84 core at https://github.com/damellis/attiny/
