# Fritzing sketch Physical-Layout_Prototype_b (saved by Fritzing 1.0.6)
circuit board: 6.27739cm x 4.33939cm
breadboards: 1

parts:
  ATTiny_84 = ATTiny84 [package=dip]
  R7 = Resistor [tolerance=±5% power=0.25W resistance=220 package=THT]
  R6 = Resistor [tolerance=±5% power=0.25W resistance=220 package=THT]
  R5 = Resistor [tolerance=±5% power=0.25W resistance=330 package=THT]
  5V = Camdenboss CTB0158-2 [part_number=CTB0158-2 package=THT]
  LM19 = Header 3 [package=jst-3-pth]
  10K_pot = Header 3 [package=jst-3-pth]
  LEDs = Header 4 [package=jst-4-pth]

nets:
  N1: ATTiny_84.pin1, 5V.pin1, LM19.1, 10K_pot.3
  N2: ATTiny_84.pin3, R7.Pin_0
  N3: ATTiny_84.pin5, R6.Pin_0
  N4: ATTiny_84.pin6, LM19.2
  N5: ATTiny_84.pin10, 10K_pot.2
  N6: ATTiny_84.pin13, R5.Pin_0
  N7: ATTiny_84.pin14, 5V.pin2, LM19.3, 10K_pot.1, LEDs.4
  N8: R7.Pin_1, LEDs.3
  N9: R6.Pin_1, LEDs.2
  N10: R5.Pin_1, LEDs.1

notes:
  TM19 Sensor IC
  10K Pot for setting desired temperature
  0.1uF
  330
  220
  5 Volts DC Power Source
  low
  mid
  high
  gnd
  +

custom parts:
  ATTiny84: Atmel ATTiny84 processor. 8 ADC pins, 4 PWM pins. Available in either 10MHz or 20MHz. The last 2 pin numbers refer to arduino. D6 = Arduino 6, A6 = Arduino A6 example: PA6 (SDA/MOSI/OC1A/DI/AD6/PCINT6/D6/A6) NOTE: This part is diagrammed to suit the MIT HLT ATTiny84 core at https://github.com/damellis/attiny/
